// Logisim project alu.circ as structural Verilog: 7 circuits, main circuit alu
module alu (
  input  [31:0] A,
  input  [31:0] B,
  input  [3:0] ALUSel,
  output [31:0] ALUResult
);

  wire comparator_1_lt;
  wire [31:0] add0, and7, mul8, mulh9, mulhu11, or6, sll1, slt2, sra13, srl5, sub12, xor4;

  Adder #(.width(32)) adder_1 (.a(A), .b(B), .out(add0));  // open: cin, cout
  Shifter #(.width(32)) shifter_1 (.in(A), .\dist (B[4:0]), .out(sll1));
  Comparator #(.width(32)) comparator_1 (.a(A), .b(B), .lt(comparator_1_lt));  // open: gt, eq
  assign xor4 = A ^ B;  // XOR_Gate xor_1, 32 bits wide
  assign slt2 = {{31{1'b0}}, comparator_1_lt};  // Bit_Extender bit_extender_1
  Shifter #(.shift("lr"), .width(32)) shifter_2 (.in(A), .\dist (B[4:0]), .out(srl5));
  assign or6 = A | B;  // OR_Gate or_1, 32 bits wide
  assign and7 = A & B;  // AND_Gate and_1, 32 bits wide
  Multiplier #(.width(32)) multiplier_1 (.a(A), .b(B), .out(mul8));  // open: cin, cout
  Multiplier #(.mode("twosComplement"), .width(32)) multiplier_2 (.a(A), .b(B), .cout(mulh9));  // open: out, cin
  Subtractor #(.width(32)) subtractor_1 (.a(A), .b(B), .out(sub12));  // open: bin, bout
  Shifter #(.shift("ar"), .width(32)) shifter_3 (.in(A), .\dist (B[4:0]), .out(sra13));
  Multiplier #(.width(32)) multiplier_3 (.a(A), .b(B), .cout(mulhu11));  // open: out, cin
  Multiplexer #(.select(4), .width(32)) multiplexer_1 (
    .in0(add0), .in1(sll1), .in2(slt2), .in4(xor4), .in5(srl5), .in6(or6), .in7(and7), .in8(mul8),
    .in9(mulh9), .in11(mulhu11), .in12(sub12), .in13(sra13), .in15(B), .out(ALUResult), .sel(ALUSel));  // open: in3, in10, in14

  // Other names for the same wires on the sheet: bsel15[31:0] = B

  // Notes on the sheet:
  //   INPUTS to your circuit
  //   0 - add
  //   1 - sll
  //   2 - slt
  //   4 - xor
  //   5 - srl
  //   6 - or
  //   7 - and
  //   8 - mul
  //   DON'T CHANGE THE LOCATIONS OF THE INPUTS AND OUTPUTS!
  //   9 - mulh
  //   12 -sub
  //   13 - sra
  //   15 - bsel
  //   11 -mulhu
  //   OUTPUT from your circuit
endmodule

module add0 (
  input  [31:0] InA,
  input  [31:0] InB,
  output [31:0] add0Out
);

  Adder #(.width(32)) adder_1 (.a(InA), .b(InB), .out(add0Out));  // open: cin, cout
endmodule

module sll1 (
  input  [31:0] InA,
  input  [4:0] InB,
  output [31:0] out_3
);

  Shifter #(.width(32)) shifter_1 (.in(InA), .\dist (InB), .out(out_3));
endmodule

module slt2 (
  input  [31:0] InA,
  input  [31:0] InB,
  output out_3
);

  Comparator #(.width(32)) comparator_1 (.a(InA), .b(InB), .lt(out_3));  // open: gt, eq
endmodule

module xor4 (
  input  [31:0] InA,
  input  [31:0] InB,
  output [31:0] out_3
);

  assign out_3 = InA ^ InB;  // XOR_Gate xor_1, 32 bits wide
endmodule

module srl5 (
  input  [31:0] InA,
  input  [4:0] InB,
  output [31:0] out_3
);

  Shifter #(.shift("lr"), .width(32)) shifter_1 (.in(InA), .\dist (InB), .out(out_3));
endmodule

module or6 (
  input  [31:0] InA,
  input  [31:0] InB,
  output [31:0] out_3
);

  or or_1 (out_3[0], InA[0], InB[0]);
  // Pins of 1 and 32 bits meet at InA
  // Pins of 1 and 32 bits meet at InB
  // Pins of 1 and 32 bits meet at out_3
endmodule
