// Logisim project control-logic.circ as structural Verilog: 1 circuit, main circuit control_logic
module control_logic (
  input  [31:0] Instruction,
  input  BrEq,
  input  BrLt,
  output PCSel,
  output RegWEn,
  output [2:0] ImmSel,
  output BrUn,
  output ASel,
  output BSel,
  output [3:0] ALUSel,
  output MemRW,
  output [1:0] WBSel
);

  wire add1, add7, addi, and1, and7, andi, B_type, beq, bge, bgeu, blt, bltu, bne, I_type, is_auipc, is_jal,
       is_jalr, is_lui, jalr, L_type, lb, lh, lw, mul1, mul7, mulh1, mulh7, mulhu1, mulhu7, not_1_out,
       not_2_out, not_3_out, or1, or7, ori, padd, paddi, pand, pandi, pbeq, pbge, pbgeu, pblt, pbltu, pbne,
       pcsbeq, pcsbge, pcsbgeu, pcsblt, pcsbltu, pcsbne, pjalr, plb, plh, plw, pmul, pmulh, pmulhu, por,
       pori, psb, psh, psll, pslli, pslri, pslt, pslti, psra, psrai, psrl, psub, psw, pxor, pxori, R_type,
       S_type, sb, sh, sll1, sll7, slli, slli7, slt1, slt7, slti, sra1, sra7, srai, srai7, srl1, srl7, srli,
       srli7, sub1, sub7, sw, xor1, xor7, xori;
  wire [5:0] priority_encoder_1_out;
  wire [15:14] rom_1_data;

  Priority_Encoder #(.select_enc(6)) priority_encoder_1 (
    .in0(padd), .in1(pmul), .in2(psub), .in3(psll), .in4(pmulh), .in5(pmulhu), .in6(pslt), .in7(pxor),
    .in8(psrl), .in9(psra), .in10(por), .in11(pand), .in12(plb), .in13(plh), .in14(plw), .in15(paddi),
    .in16(pslli), .in17(pslti), .in18(pxori), .in19(pslri), .in20(psrai), .in21(pori), .in22(pandi),
    .in23(psb), .in24(psh), .in25(psw), .in26(pbeq), .in27(pbne), .in28(pblt), .in29(pbge), .in30(pbltu),
    .in31(pbgeu), .in32(is_auipc), .in33(is_lui), .in34(is_jal), .in35(pjalr), .out(priority_encoder_1_out));  // open: in36, in37, in38, in39, in40, in41, in42, in43, in44, in45, in46, in47, in48, in49, in50, in51, in52, in53, in54, in55, in56, in57, in58, in59, in60, in61, in62, in63, gs, en_out, en_in
  Comparator #(.width(3)) comparator_1 (.a(3'b000), .b(Instruction[14:12]), .eq(addi));  // open: gt, lt
  Comparator #(.width(3)) comparator_2 (.a(3'b111), .b(Instruction[14:12]), .eq(andi));  // open: gt, lt
  Comparator #(.width(3)) comparator_3 (.a(3'b110), .b(Instruction[14:12]), .eq(ori));  // open: gt, lt
  Comparator #(.width(3)) comparator_4 (.a(3'b100), .b(Instruction[14:12]), .eq(xori));  // open: gt, lt
  Comparator #(.width(3)) comparator_5 (.a(3'b001), .b(Instruction[14:12]), .eq(slli));  // open: gt, lt
  Comparator #(.width(3)) comparator_6 (.a(3'b101), .b(Instruction[14:12]), .eq(srli));  // open: gt, lt
  Comparator #(.width(3)) comparator_7 (.a(3'b101), .b(Instruction[14:12]), .eq(srai));  // open: gt, lt
  Comparator #(.width(3)) comparator_8 (.a(3'b010), .b(Instruction[14:12]), .eq(slti));  // open: gt, lt
  Comparator #(.width(7)) comparator_9 (.a({7{1'b0}}), .b(Instruction[31:25]), .eq(slli7));  // open: gt, lt
  Comparator #(.width(7)) comparator_10 (.a({7{1'b0}}), .b(Instruction[31:25]), .eq(srli7));  // open: gt, lt
  Comparator #(.width(7)) comparator_11 (.a(7'b0100000), .b(Instruction[31:25]), .eq(srai7));  // open: gt, lt
  Comparator #(.width(3)) comparator_12 (.a(3'b000), .b(Instruction[14:12]), .eq(beq));  // open: gt, lt
  Comparator #(.width(3)) comparator_13 (.a(3'b101), .b(Instruction[14:12]), .eq(bge));  // open: gt, lt
  Comparator #(.width(3)) comparator_14 (.a(3'b111), .b(Instruction[14:12]), .eq(bgeu));  // open: gt, lt
  Comparator #(.width(3)) comparator_15 (.a(3'b100), .b(Instruction[14:12]), .eq(blt));  // open: gt, lt
  Comparator #(.width(3)) comparator_16 (.a(3'b110), .b(Instruction[14:12]), .eq(bltu));  // open: gt, lt
  Comparator #(.width(3)) comparator_17 (.a(3'b001), .b(Instruction[14:12]), .eq(bne));  // open: gt, lt
  ROM #(.addrWidth(6), .dataWidth(16)) rom_1 (
    .addr(priority_encoder_1_out), .data({rom_1_data, WBSel, MemRW, ALUSel, BSel, ASel, BrUn, ImmSel, RegWEn}));
  Comparator #(.width(7)) comparator_18 (.a(7'b0010011), .b(Instruction[6:0]), .eq(I_type));  // open: gt, lt
  Comparator #(.width(7)) comparator_19 (.a(7'b0110011), .b(Instruction[6:0]), .eq(R_type));  // open: gt, lt
  Comparator #(.width(7)) comparator_20 (.a(7'b1100011), .b(Instruction[6:0]), .eq(B_type));  // open: gt, lt
  Comparator #(.width(7)) comparator_21 (.a(7'b0000011), .b(Instruction[6:0]), .eq(L_type));  // open: gt, lt
  Comparator #(.width(7)) comparator_22 (.a(7'b0100011), .b(Instruction[6:0]), .eq(S_type));  // open: gt, lt
  Comparator #(.width(7)) comparator_23 (.a(7'b0010111), .b(Instruction[6:0]), .eq(is_auipc));  // open: gt, lt
  Comparator #(.width(7)) comparator_24 (.a(7'b0110111), .b(Instruction[6:0]), .eq(is_lui));  // open: gt, lt
  Comparator #(.width(7)) comparator_25 (.a(7'b1101111), .b(Instruction[6:0]), .eq(is_jal));  // open: gt, lt
  Comparator #(.width(7)) comparator_26 (.a(7'b1100111), .b(Instruction[6:0]), .eq(is_jalr));  // open: gt, lt
  and and_1 (paddi, I_type, addi);
  and and_2 (pandi, I_type, andi);
  and and_3 (pori, I_type, ori);
  and and_4 (pxori, I_type, xori);
  and and_5 (pslli, I_type, slli, slli7);
  and and_6 (pslri, I_type, srli, srli7);
  and and_7 (psrai, I_type, srai, srai7);
  and and_8 (pslti, I_type, slti);
  and and_9 (pbeq, B_type, beq);
  and and_10 (pbge, B_type, bge);
  and and_11 (pbgeu, B_type, bgeu);
  and and_12 (pblt, B_type, blt);
  and and_13 (pbltu, B_type, bltu);
  and and_14 (pbne, B_type, bne);
  not not_1 (not_1_out, BrEq);
  not not_2 (not_2_out, BrLt);
  not not_3 (not_3_out, BrLt);
  Comparator #(.width(3)) comparator_27 (.a(3'b000), .b(Instruction[14:12]), .eq(add1));  // open: gt, lt
  Comparator #(.width(3)) comparator_28 (.a(3'b000), .b(Instruction[14:12]), .eq(sub1));  // open: gt, lt
  Comparator #(.width(3)) comparator_29 (.a(3'b111), .b(Instruction[14:12]), .eq(and1));  // open: gt, lt
  Comparator #(.width(3)) comparator_30 (.a(3'b110), .b(Instruction[14:12]), .eq(or1));  // open: gt, lt
  Comparator #(.width(3)) comparator_31 (.a(3'b100), .b(Instruction[14:12]), .eq(xor1));  // open: gt, lt
  Comparator #(.width(3)) comparator_32 (.a(3'b101), .b(Instruction[14:12]), .eq(srl1));  // open: gt, lt
  Comparator #(.width(3)) comparator_33 (.a(3'b101), .b(Instruction[14:12]), .eq(sra1));  // open: gt, lt
  Comparator #(.width(3)) comparator_34 (.a(3'b010), .b(Instruction[14:12]), .eq(slt1));  // open: gt, lt
  Comparator #(.width(3)) comparator_35 (.a(3'b000), .b(Instruction[14:12]), .eq(mul1));  // open: gt, lt
  Comparator #(.width(3)) comparator_36 (.a(3'b001), .b(Instruction[14:12]), .eq(mulh1));  // open: gt, lt
  Comparator #(.width(3)) comparator_37 (.a(3'b011), .b(Instruction[14:12]), .eq(mulhu1));  // open: gt, lt
  Comparator #(.width(3)) comparator_38 (.a(3'b001), .b(Instruction[14:12]), .eq(sll1));  // open: gt, lt
  Comparator #(.width(7)) comparator_39 (.a({7{1'b0}}), .b(Instruction[31:25]), .eq(add7));  // open: gt, lt
  Comparator #(.width(7)) comparator_40 (.a(7'b0100000), .b(Instruction[31:25]), .eq(sub7));  // open: gt, lt
  Comparator #(.width(7)) comparator_41 (.a({7{1'b0}}), .b(Instruction[31:25]), .eq(and7));  // open: gt, lt
  Comparator #(.width(7)) comparator_42 (.a({7{1'b0}}), .b(Instruction[31:25]), .eq(or7));  // open: gt, lt
  Comparator #(.width(7)) comparator_43 (.a({7{1'b0}}), .b(Instruction[31:25]), .eq(xor7));  // open: gt, lt
  Comparator #(.width(7)) comparator_44 (.a({7{1'b0}}), .b(Instruction[31:25]), .eq(sll7));  // open: gt, lt
  Comparator #(.width(7)) comparator_45 (.a({7{1'b0}}), .b(Instruction[31:25]), .eq(srl7));  // open: gt, lt
  Comparator #(.width(7)) comparator_46 (.a(7'b0000001), .b(Instruction[31:25]), .eq(mulhu7));  // open: gt, lt
  Comparator #(.width(7)) comparator_47 (.a(7'b0100000), .b(Instruction[31:25]), .eq(sra7));  // open: gt, lt
  Comparator #(.width(7)) comparator_48 (.a({7{1'b0}}), .b(Instruction[31:25]), .eq(slt7));  // open: gt, lt
  Comparator #(.width(7)) comparator_49 (.a(7'b0000001), .b(Instruction[31:25]), .eq(mul7));  // open: gt, lt
  Comparator #(.width(7)) comparator_50 (.a(7'b0000001), .b(Instruction[31:25]), .eq(mulh7));  // open: gt, lt
  and and_15 (pcsbeq, pbeq, BrEq);
  and and_16 (pcsbne, pbne, not_1_out);
  and and_17 (pcsblt, pblt, BrLt);
  and and_18 (pcsbge, pbge, not_2_out);
  and and_19 (pcsbltu, pbltu, BrLt, BrUn);
  and and_20 (pcsbgeu, pbgeu, not_3_out, BrUn);
  and and_21 (padd, R_type, add1, add7);
  and and_22 (psub, R_type, sub1, sub7);
  and and_23 (pand, R_type, and1, and7);
  and and_24 (por, R_type, or1, or7);
  and and_25 (pxor, R_type, xor1, xor7);
  and and_26 (psll, R_type, sll1, sll7);
  and and_27 (psrl, R_type, srl1, srl7);
  and and_28 (psra, R_type, sra1, sra7);
  and and_29 (pslt, R_type, slt1, slt7);
  and and_30 (pmul, R_type, mul1, mul7);
  and and_31 (pmulh, R_type, mulh1, mulh7);
  and and_32 (pmulhu, R_type, mulhu1, mulhu7);
  or or_1 (PCSel, is_jal, is_jalr, pcsbeq, pcsbne, pcsblt, pcsbge, pcsbltu, pcsbgeu);
  Comparator #(.width(3)) comparator_51 (.a(3'b000), .b(Instruction[14:12]), .eq(lb));  // open: gt, lt
  Comparator #(.width(3)) comparator_52 (.a(3'b001), .b(Instruction[14:12]), .eq(lh));  // open: gt, lt
  Comparator #(.width(3)) comparator_53 (.a(3'b010), .b(Instruction[14:12]), .eq(lw));  // open: gt, lt
  Comparator #(.width(3)) comparator_54 (.a(3'b000), .b(Instruction[14:12]), .eq(sb));  // open: gt, lt
  Comparator #(.width(3)) comparator_55 (.a(3'b001), .b(Instruction[14:12]), .eq(sh));  // open: gt, lt
  Comparator #(.width(3)) comparator_56 (.a(3'b010), .b(Instruction[14:12]), .eq(sw));  // open: gt, lt
  Comparator #(.width(3)) comparator_57 (.a(3'b000), .b(Instruction[14:12]), .eq(jalr));  // open: gt, lt
  and and_33 (plb, L_type, lb);
  and and_34 (plh, L_type, lh);
  and and_35 (plw, L_type, lw);
  and and_36 (psb, S_type, sb);
  and and_37 (psh, S_type, sh);
  and and_38 (psw, S_type, sw);
  and and_39 (pjalr, is_jalr, jalr);

  // Notes on the sheet:
  //   PE for unique instruction
  //   INPUTS to your circuit
  //   Connect ROM Input here ->
  //   I-Type func3
  //   I-Type func7
  //   B-Type func3
  //   contents of rom_1 (hex, n*v repeats v):
  //   1 401 601 81 481 581 101 201 281 681 301 381 1041 1041 1041 41 c1 141 241 2c1 6c1 341 3c1 842 842
  //   842 4*64 74 74 67 7c7 2069 2041
  //   Opcode differentiation
  //   ROM FOR CONTROL LOGIC
  //   I-Type PE Logic
  //   B-Type PE Logic
  //   DON'T CHANGE THE LOCATIONS OF THE INPUTS AND OUTPUTS!
  //   This is only if you choose to do the ROM option
  //   CONNECT
  //   WIRE
  //   TO
  //   USE
  //   ROM
  //   OUTPUT from your circuit
  //   R-Type func3
  //   R-Type func7
  //   Reminder: If using ROM, use combinational logic for PCSel
  //   PCSel Logic
  //   R-Type PE Logic
  //   L-Type func3
  //   S-Type func3
  //   J-Type func3
  //   L-Type PE Logic
  //   S-Type PE Logic
  //   S-Type PE Logic
endmodule
