// Logisim project cpu.circ as structural Verilog: 1 circuit, main circuit cpu
module cpu (
  input  clk,
  input  [31:0] Instruction,
  input  [31:0] MemReadData,
  output [31:0] MemAddress,
  output [31:0] ProgramCounter,
  output [31:0] ra,
  output [31:0] sp,
  output [31:0] t0,
  output [31:0] t1,
  output [31:0] t2,
  output [31:0] s0,
  output [31:0] s1,
  output [31:0] a0,
  output [3:0] MemWriteMask,
  output [31:0] MemWriteData
);

  wire ASel, BrEq, BrLt, BrUn, BSel, MemRW, PCSel, RegWEn;
  wire [1:0] WBSel;
  wire [2:0] ImmSel;
  wire [3:0] ALUSel;
  wire [7:0] adder_2_out, num_cycles_q;
  wire [31:0] DataToReg, exi, expc, expcp4, Immediate, multiplexer_1_out, multiplexer_2_out,
       multiplexer_3_out, multiplexer_4_out, pcp4, ReadData1, ReadData2, WriteData;

  Adder #(.width(32)) adder_1 (.a(ProgramCounter), .b(32'h4), .out(pcp4));  // open: cin, cout
  Multiplexer #(.width(32)) multiplexer_1 (.in0(pcp4), .in1(MemAddress), .out(multiplexer_1_out), .sel(PCSel));
  // Probe on PCSel
  // Probe on exi
  Register #(.width(32)) PC (.D(multiplexer_1_out), .clk(clk), .Q(ProgramCounter));  // open: en, clr
  Register num_cycles (.D(adder_2_out), .clk(clk), .Q(num_cycles_q));  // open: en, clr
  Adder adder_2 (.a(num_cycles_q), .b(8'h1), .out(adder_2_out));  // open: cin, cout
  Register #(.width(32)) register_1 (.D(ProgramCounter), .clk(clk), .Q(expc));  // open: en, clr
  // Probe on ImmSel
  Register #(.width(32)) register_2 (.D(pcp4), .clk(clk), .Q(expcp4));  // open: en, clr
  // Probe on exi[19:15]
  // Probe on exi[24:20]
  // Probe on exi[11:7]
  // Probe on WriteData
  // Probe on RegWEn
  control_logic control_logic_1 (
    .Instruction(exi), .BrEq(BrEq), .BrLt(BrLt), .PCSel(PCSel), .RegWEn(RegWEn), .ImmSel(ImmSel),
    .BrUn(BrUn), .ASel(ASel), .BSel(BSel), .ALUSel(ALUSel), .MemRW(MemRW), .WBSel(WBSel));
  imm_gen imm_gen_1 (.Instruction(exi), .ImmSel(ImmSel), .Immediate(Immediate));
  // Probe on Immediate
  regfile regfile_1 (
    .ReadIndex1(exi[19:15]), .ReadIndex2(exi[24:20]), .WriteIndex(exi[11:7]), .WriteData(WriteData),
    .RegWEn(RegWEn), .clk(clk), .ra(ra), .sp(sp), .t0(t0), .t1(t1), .t2(t2), .s0(s0), .s1(s1), .a0(a0),
    .ReadData1(ReadData1), .ReadData2(ReadData2));
  // Probe on ReadData1
  // Probe on ReadData2
  Register #(.width(32)) register_3 (.D(multiplexer_2_out), .clk(clk), .Q(exi));  // open: en, clr
  Multiplexer #(.width(32)) multiplexer_2 (.in0(Instruction), .in1(32'h13), .out(multiplexer_2_out), .sel(PCSel));
  // Probe on BrUn
  Multiplexer #(.width(32)) multiplexer_3 (.in0(ReadData1), .in1(expc), .out(multiplexer_3_out), .sel(ASel));
  Multiplexer #(.width(32)) multiplexer_4 (.in0(ReadData2), .in1(Immediate), .out(multiplexer_4_out), .sel(BSel));
  alu alu_1 (.A(multiplexer_3_out), .B(multiplexer_4_out), .ALUSel(ALUSel), .ALUResult(MemAddress));
  // Probe on ALUSel
  // Probe on BrEq
  branch_comp branch_comp_1 (.BrData1(ReadData1), .BrData2(ReadData2), .BrUn(BrUn), .BrEq(BrEq), .BrLt(BrLt));
  // Probe on BrLt
  // Probe on MemAddress
  Multiplexer #(.select(2), .width(32)) multiplexer_5 (
    .in0(MemAddress), .in1(DataToReg), .in2(expcp4), .out(WriteData), .sel(WBSel));  // open: in3
  // Probe on WBSel
  // Probe on MemRW
  partial_store partial_store_1 (
    .Instruction(exi), .MemAddress(MemAddress), .DataFromReg(ReadData2), .MemRW(MemRW),
    .MemWriteMask(MemWriteMask), .DataToMem(MemWriteData));
  partial_load partial_load_1 (
    .Instruction(exi), .MemAddress(MemAddress), .DataFromMem(MemReadData), .DataToReg(DataToReg));

  // Other names for the same wires on the sheet: ALUResult[31:0] = MemAddress; WriteIndex[4:0] = exi[11:7];
  //   ReadIndex1[4:0] = exi[19:15]; ReadIndex2[4:0] = exi[24:20]

  // Notes on the sheet:
  //   To IMEM
  //   IMEM (do **NOT** move this)
  //   From IMEM
  //   Inputs/Outputs for testing. Do **NOT** move these.
  //   It is OK to move the PC, RegFile, ALU, MEM, Branch Comp, Imm Gen, Partial Load, Partial Store and Control Logic to wherever is most convenient for you when constructing your CPU, and to delete this text
  //   To DMEM
  //   DMEM (do **NOT** move this)
  //   From DMEM
endmodule
