// Logisim project imm-gen.circ as structural Verilog: 1 circuit, main circuit imm_gen
module imm_gen (
  input  [31:0] Instruction,
  input  [2:0] ImmSel,
  output [31:0] Immediate
);

  wire [31:0] bit_extender_4_out, I_type_Imm, J_type_Imm, S_type_Imm, U_type_Imm;
  wire [31:12] B_type_Imm;

  assign I_type_Imm = {{20{Instruction[31]}}, Instruction[31:20]};  // Bit_Extender bit_extender_1
  assign B_type_Imm = {{19{Instruction[31]}}, Instruction[31]};  // Bit_Extender bit_extender_2
  assign S_type_Imm = {{20{Instruction[31]}}, {Instruction[31:25], Instruction[11:7]}};  // Bit_Extender bit_extender_3
  assign bit_extender_4_out = {{12{1'b0}}, Instruction[31:12]};  // Bit_Extender bit_extender_4
  assign J_type_Imm = {{11{Instruction[31]}}, {Instruction[31], Instruction[19:12], Instruction[20], Instruction[30:21], 1'b0}};  // Bit_Extender bit_extender_5
  Shifter #(.width(32)) shifter_1 (.in(bit_extender_4_out), .\dist (5'b01100), .out(U_type_Imm));
  Multiplexer #(.select(3), .width(32)) multiplexer_1 (
    .in0(I_type_Imm), .in1(S_type_Imm),
    .in2({B_type_Imm, Instruction[7], Instruction[30:25], Instruction[11:8], 1'b0}), .in3(U_type_Imm),
    .in4(J_type_Imm), .out(Immediate), .sel(ImmSel));  // open: in5, in6, in7

  // Other names for the same wires on the sheet: B_type_Imm[11:1] = {Instruction[7], Instruction[30:25], Instruction[11:8]}

  // Notes on the sheet:
  //   INPUTS to your circuit
  //   DON'T CHANGE THE LOCATIONS OF THE INPUTS AND OUTPUTS!
  //   OUTPUT from your circuit
endmodule
