// Logisim project partial-load.circ as structural Verilog: 1 circuit, main circuit partial_load
module partial_load (
  input  [31:0] Instruction,
  input  [31:0] MemAddress,
  input  [31:0] DataFromMem,
  output [31:0] DataToReg
);

  wire [2:0] adder_1_out, multiplexer_3_out;
  wire [31:0] bit_extender_1_out, bit_extender_2_out, bit_extender_3_out, bit_extender_4_out,
       bit_extender_5_out, bit_extender_6_out, bit_extender_7_out, bit_extender_8_out, bit_extender_9_out,
       bit_extender_10_out, bit_extender_11_out, bit_extender_12_out, bit_extender_13_out,
       bit_extender_14_out, lb, lh;

  assign bit_extender_1_out = {{24{DataFromMem[7]}}, DataFromMem[7:0]};  // Bit_Extender bit_extender_1
  assign bit_extender_2_out = {{24{DataFromMem[15]}}, DataFromMem[15:8]};  // Bit_Extender bit_extender_2
  assign bit_extender_3_out = {{24{DataFromMem[23]}}, DataFromMem[23:16]};  // Bit_Extender bit_extender_3
  assign bit_extender_4_out = {{24{DataFromMem[31]}}, DataFromMem[31:24]};  // Bit_Extender bit_extender_4
  assign bit_extender_5_out = {{16{DataFromMem[15]}}, DataFromMem[15:0]};  // Bit_Extender bit_extender_5
  assign bit_extender_6_out = {{16{DataFromMem[23]}}, DataFromMem[23:8]};  // Bit_Extender bit_extender_6
  assign bit_extender_7_out = {{16{DataFromMem[31]}}, DataFromMem[31:16]};  // Bit_Extender bit_extender_7
  Multiplexer #(.select(2), .width(32)) multiplexer_1 (
    .in0(bit_extender_1_out), .in1(bit_extender_2_out), .in2(bit_extender_3_out), .in3(bit_extender_4_out),
    .out(lb), .sel(MemAddress[1:0]));
  Multiplexer #(.select(2), .width(32)) multiplexer_2 (
    .in0(bit_extender_5_out), .in1(bit_extender_6_out), .in2(bit_extender_7_out), .out(lh),
    .sel(MemAddress[1:0]));  // open: in3
  assign bit_extender_8_out = {{24{DataFromMem[7]}}, DataFromMem[7:0]};  // Bit_Extender bit_extender_8
  assign bit_extender_9_out = {{24{DataFromMem[15]}}, DataFromMem[15:8]};  // Bit_Extender bit_extender_9
  assign bit_extender_10_out = {{24{DataFromMem[23]}}, DataFromMem[23:16]};  // Bit_Extender bit_extender_10
  assign bit_extender_11_out = {{24{DataFromMem[31]}}, DataFromMem[31:24]};  // Bit_Extender bit_extender_11
  assign bit_extender_12_out = {{16{DataFromMem[15]}}, DataFromMem[15:0]};  // Bit_Extender bit_extender_12
  assign bit_extender_13_out = {{16{DataFromMem[23]}}, DataFromMem[23:8]};  // Bit_Extender bit_extender_13
  assign bit_extender_14_out = {{16{DataFromMem[31]}}, DataFromMem[31:16]};  // Bit_Extender bit_extender_14
  Adder #(.width(3)) adder_1 (
    .a({Instruction[12], 2'b00}), .b({1'b0, MemAddress[1:0]}), .out(adder_1_out));  // open: cin, cout
  Multiplexer #(.width(3)) multiplexer_3 (
    .in0(adder_1_out), .in1(3'b111), .out(multiplexer_3_out), .sel(Instruction[13]));
  Multiplexer #(.select(2), .width(32)) multiplexer_4 (
    .in0(lb), .in1(lh), .in2(DataFromMem), .out(DataToReg), .sel(Instruction[13:12]));  // open: in3

  // Other names for the same wires on the sheet: lb00[7:0] = DataFromMem[7:0]; lh00[15:0] = DataFromMem[15:0];
  //   lb01[7:0] = DataFromMem[15:8]; lh01[15:0] = DataFromMem[23:8]; lb10[7:0] = DataFromMem[23:16];
  //   lh10[15:0] = DataFromMem[31:16]; lb11[7:0] = DataFromMem[31:24]

  // Notes on the sheet:
  //   INPUTS to your circuit
  //   DON'T CHANGE THE LOCATIONS OF THE INPUTS AND OUTPUTS!
  //   OUTPUT from your circuit
endmodule
