// Logisim project partial-store.circ as structural Verilog: 1 circuit, main circuit partial_store
module partial_store (
  input  [31:0] Instruction,
  input  [31:0] MemAddress,
  input  [31:0] DataFromReg,
  input  MemRW,
  output [3:0] MemWriteMask,
  output [31:0] DataToMem
);

  wire [1:0] adder_1_out, multiplier_1_out;
  wire [3:0] multiplexer_1_out;
  wire [4:0] bott2, multiplier_2_out;
  wire [31:0] bit_extender_2_out, bit_extender_3_out, sb, sh;

  Adder #(.width(2)) adder_1 (.a(Instruction[13:12]), .b(2'b01), .out(adder_1_out));  // open: cin, cout
  Multiplier #(.width(2)) multiplier_1 (.a(adder_1_out), .b({1'b0, MemRW}), .out(multiplier_1_out));  // open: cin, cout
  Multiplexer #(.select(2), .width(4)) multiplexer_1 (
    .in0(4'b0000), .in1(4'b0001), .in2(4'b0011), .in3(4'b1111), .out(multiplexer_1_out),
    .sel(multiplier_1_out));
  assign bott2 = {{3{1'b0}}, MemAddress[1:0]};  // Bit_Extender bit_extender_1
  assign bit_extender_2_out = {{24{1'b0}}, DataFromReg[7:0]};  // Bit_Extender bit_extender_2
  Multiplier #(.width(5)) multiplier_2 (.a(bott2), .b(5'b01000), .out(multiplier_2_out));  // open: cin, cout
  assign bit_extender_3_out = {{16{1'b0}}, DataFromReg[15:0]};  // Bit_Extender bit_extender_3
  Multiplexer #(.select(2), .width(32)) multiplexer_2 (
    .in0(sb), .in1(sh), .in2(DataFromReg), .out(DataToMem), .sel(Instruction[13:12]));  // open: in3
  Shifter #(.width(32)) shifter_1 (.in(bit_extender_2_out), .\dist (multiplier_2_out), .out(sb));
  Shifter #(.width(32)) shifter_2 (.in(bit_extender_3_out), .\dist (multiplier_2_out), .out(sh));
  Shifter #(.width(4)) shifter_3 (.in(multiplexer_1_out), .\dist (MemAddress[1:0]), .out(MemWriteMask));

  // Notes on the sheet:
  //   INPUTS to your circuit
  //   DON'T CHANGE THE LOCATIONS OF THE INPUTS AND OUTPUTS!
  //   OUTPUT from your circuit
endmodule
